// Logisim project Added.circ as structural Verilog: 1 circuit, main circuit AddedInp
// AddInp
module AddedInp (
  input  [31:0] A,
  input  [31:0] B,
  output SA,
  output SB,
  output [31:0] to_normalize,
  output Cout,
  output Sign_bit,
  output [10:0] Exp_Large,
  output SAxorSB,
  output A_B,
  output Flag
);

  wire inputhandle_1_switch, n7486_1_p5, n7486_1_p11;
  wire [10:0] inputhandle_1_expdiff, inputprocess_1_exp, inputprocess_2_exp;
  wire [31:0] inputhandle_1_large, inputhandle_1_small, inputprocess_1_frac, inputprocess_2_frac,
       n2compl32_1_o, n2compl32_2_o, n32adder_1_s, n32mux2x1_1_o, rigthshiftwithempty_1_o;

  InputProcess inputprocess_1 (.in_1(A), .Sign(SA), .Exp(inputprocess_1_exp), .Frac(inputprocess_1_frac));
  InputProcess inputprocess_2 (.in_1(B), .Sign(SB), .Exp(inputprocess_2_exp), .Frac(inputprocess_2_frac));
  InputHandle inputhandle_1 (
    .SA(SA), .SB(SB), .Fraction1(inputprocess_1_frac), .Fraction2(inputprocess_2_frac),
    .A_Exp(inputprocess_1_exp), .B_Exp(inputprocess_2_exp), .A_B(A_B), .Switch(inputhandle_1_switch),
    .Large(inputhandle_1_large), .Small(inputhandle_1_small), .ExpDiff(inputhandle_1_expdiff),
    .Exp_Large(Exp_Large));
  // _7486 7486_1: pin names not known; wires that end beside it: SB, SA, SAxorSB, inputhandle_1_switch, n7486_1_p5, Sign_bit, 1'b0, 1'b1, 1'b1, Cout, n7486_1_p11
  // _7408 7408_1: pin names not known; wires that end beside it: 1'b1, SAxorSB, n7486_1_p11, n7486_1_p5, 1'b0
  RigthShiftWithEmpty rigthshiftwithempty_1 (
    .A(inputhandle_1_small), .in_2(inputhandle_1_expdiff), .O(rigthshiftwithempty_1_o));
  _2Compl32 u_2compl32_1 (.A(rigthshiftwithempty_1_o), .O(n2compl32_1_o));
  _32Is0 u_32is0_1 (.A(rigthshiftwithempty_1_o), .Flag(Flag));
  _32Mux2X1 u_32mux2x1_1 (
    .A(rigthshiftwithempty_1_o), .B(n2compl32_1_o), .E_prime(1'b0), .S(SAxorSB), .O(n32mux2x1_1_o));
  _32Adder u_32adder_1 (.A(inputhandle_1_large), .B(n32mux2x1_1_o), .Cin(1'b0), .S(n32adder_1_s), .Cout(Cout));
  _2Compl32 u_2compl32_2 (.A(n32adder_1_s), .O(n2compl32_2_o));
  _32Mux2X1 u_32mux2x1_2 (.A(n32adder_1_s), .B(n2compl32_2_o), .E_prime(1'b0), .S(n7486_1_p5), .O(to_normalize));

  // Notes on the sheet:
  //   actual sign
  //   sign
  //   switch
  //   Cout'
  //   sign
  //   Cout
endmodule
