// Logisim project NormalizerLib.circ as structural Verilog: 1 circuit, main circuit Normalization
// Normalize
module Normalization (
  input  SA,
  input  SB,
  input  [31:0] I,
  input  [10:0] Exp,
  input  Cout,
  input  S1xorS2,
  output Valid,
  output [31:0] Out,
  output [10:0] Add_with_exp
);

  wire n11is0_1_o, n7404_1_p4, n7432_1_p3, n7486_1_p5, shiftfinder_1_va;
  wire [4:0] shiftfinder_1_o;
  wire [10:0] n2compl11_1_o, n5to11_1_o, n5to11_2_o;
  wire [31:0] arbleftshift_1_o, n1leftshift_1_o, n32mux2x1_1_o;

  ShiftFinder shiftfinder_1 (.I(I), .Va(shiftfinder_1_va), .O(shiftfinder_1_o));
  _1LeftShift u_1leftshift_1 (.A(I), .S(1'b1), .O(n1leftshift_1_o));
  ArbLeftShift arbleftshift_1 (.A(n1leftshift_1_o), .C(shiftfinder_1_o), .O(arbleftshift_1_o));
  _32Mux2X1 u_32mux2x1_1 (.A(n1leftshift_1_o), .B(I), .E_prime(1'b0), .S(Cout), .O(n32mux2x1_1_o));
  _32Mux2X1 u_32mux2x1_2 (.A(n32mux2x1_1_o), .B(arbleftshift_1_o), .E_prime(1'b0), .S(S1xorS2), .O(Out));
  _5to11 u_5to11_1 (.A(shiftfinder_1_o), .O(n5to11_1_o));
  // _7486 7486_1: pin names not known; wires that end beside it: 1'b0, 1'b1, SA, SB, n7486_1_p5
  _5to11 u_5to11_2 (.A({4'b0000, Cout}), .O(n5to11_2_o));
  _2Compl11 u_2compl11_1 (.A(n5to11_1_o), .O(n2compl11_1_o));
  // _7404 7404_1: pin names not known; wires that end beside it: 1'b0, 1'b1, n7486_1_p5, n7404_1_p4
  _11Mux2X1 u_11mux2x1_1 (.A(n5to11_2_o), .B(n2compl11_1_o), .E_prime(1'b0), .S(S1xorS2), .O(Add_with_exp));
  _11Is0 u_11is0_1 (.A(Exp), .O(n11is0_1_o));
  // _7432 7432_1: pin names not known; wires that end beside it: shiftfinder_1_va, n7404_1_p4, n7432_1_p3, 1'b0, 1'b1, 1'b1
  // _7408 7408_1: pin names not known; wires that end beside it: 1'b0, 1'b1, n7432_1_p3, n11is0_1_o, Valid
endmodule
